# Fritzing sketch floggr (saved by Fritzing 0.7.4b)
breadboards: 1

parts:
  Arduino1 = Arduino  # not connected
  Part1 = Arduino GPS Shield
  Part2 = Barometric Pressure Sensor - BMP085 Breakout
  Part3 = OpenLog
  S1 = Pushbutton [package="[THT]"]
  R1 = Resistor [tolerance=±5% resistance=10k package=THT]
  VCC1 = Battery  # not connected
  Part4 = Humidity Temperature Sensor SHT15  # not connected
  Part5 = Triple Axis Magnetometer - HMC5883 Breakout  # not connected
  Part6 = Ambient Light Sensor (TEMT6000 Breakout Board)  # not connected

nets:
  GND: Part1.D10, Part1.GND, Part2.GND, Part3.GND, R1.Pin_0
  N1: Part1.D11, Part1.5VIN, Part3.VCC, S1.Pin_1, S1.Pin_2
  N2: Part1.D12, Part3.TXO
  N3: Part1.D13, Part3.RXI
  N4: Part1.A4, Part2.SDA
  N5: Part1.A5, Part2.SCL
  N6: Part1.D6, S1.Pin_3, S1.Pin_4, R1.Pin_1
  N7: Part2.VCC, Part2.XCLR

notes:
  Main components:
  - Arduino Uno
  - GPS EMP406A
  - SD card breakout
  - BMP085 Barometer
  - simple switch
  - 6 x AA batteries
  NB Sparkfun SD card breakout board was used, not OpenLog
  CS <-> D10
  DI <-> D11
  VCC <-> 5V rail
  CLK <-> D13
  GND <-> GND
  D0 <-> D12
  IRQ - not used
  P9 - not used
  CD - not used
  WP - not used
  COM - not used
  Optional alternative sensors:
  - Humidity
  - Magenetometer
  - Ambient light
